# Fritzing sketch REX_Trial_UltrasonicMeasure (saved by Fritzing 0.9.5d)
breadboards: 1

parts:
  Part1 = Arduino Uno (Rev3)
  HC-SR04_Sensor_1 = HC-SR04 Ultrasonic Distance Sensor
  LED1 = LED - 5mm [color="Red (633nm)" package="5 mm [THT]"]
  R1 = Resistor [tolerance=±5% resistance=220 package=THT]

nets:
  N1: Part1.D2, HC-SR04_Sensor_1.TRIG
  N2: Part1.D3_PWM, HC-SR04_Sensor_1.ECHO
  N3: Part1.D6_PWM, R1.Pin_1
  5V: Part1.5V, HC-SR04_Sensor_1.VCC
  GND: Part1.GND, HC-SR04_Sensor_1.GND, LED1.anode
  N4: LED1.cathode, R1.Pin_0
