# Fritzing sketch REX_Trial_UltrasonicMeasure (saved by Fritzing 0.9.5d)
breadboards: 1

parts:
  Part1 = Arduino Uno (Rev3)
  HC-SR04_Sensor_1 = HC-SR04 Ultrasonic Distance Sensor
  R1 = Resistor [tolerance=±5% resistance=220 package=THT]
  buz1 = Piezo Buzzer

nets:
  N1: Part1.D2, HC-SR04_Sensor_1.TRIG
  N2: Part1.D3_PWM, HC-SR04_Sensor_1.ECHO
  N3: Part1.D6_PWM, R1.Pin_1
  5V: Part1.5V, HC-SR04_Sensor_1.VCC
  GND: Part1.GND, HC-SR04_Sensor_1.GND, buz1.pin_1
  N4: R1.Pin_0, buz1.pin_2

custom parts:
  Piezo Buzzer: Part from https://www.nutsvolts.com/magazine/article/november2012_SmileysWorkshop modified to be .3 in spacing to match the adafruit buzzer 5V breadboard friendly part.
